# Fritzing sketch truhialarmv3_minimal (saved by Fritzing 0.9.3b)
breadboards: 1

parts:
  J1 = female pin header, 8 pins [form="♀ (female)"]
  J2 = female pin header, 8 pins [form="♀ (female)"]
  J3 = double row female pin header, 2 pins [form="♀ (female)"]

nets:
  GND: J1.pin1
  N1: J1.pin8, J2.pin4, J2.pin8
  N2: J2.pin1, J3.pin1
  N3: J2.pin7, J3.pin2

notes:
  CH340
  ESP-01
  Sensor
